// Logisim project 32BitMemoryLocation.circ as structural Verilog
module _1BitMemLocation (
  input  Input,
  input  Clock,
  input  Enabled,
  output out_4
);

  wire not_1_out;

  not not_1 (not_1_out, Input);
  J_K_Flip_Flop j_k_ff_1 (.J(Input), .clk(Clock), .K(not_1_out), .Q(out_4), .en(Enabled));  // open: Qn, preset, reset
endmodule

module _8BitMemLocation (
  input  [7:0] in_1,
  input  Clock,
  input  Enabled,
  output [7:0] Memory
);

  _1BitMemLocation u_1bitmemlocation_1 (.Input(in_1[7]), .Clock(Clock), .out_4(Memory[7]), .Enabled(Enabled));
  _1BitMemLocation u_1bitmemlocation_2 (.Input(in_1[6]), .Clock(Clock), .out_4(Memory[6]), .Enabled(Enabled));
  _1BitMemLocation u_1bitmemlocation_3 (.Input(in_1[5]), .Clock(Clock), .out_4(Memory[5]), .Enabled(Enabled));
  _1BitMemLocation u_1bitmemlocation_4 (.Input(in_1[4]), .Clock(Clock), .out_4(Memory[4]), .Enabled(Enabled));
  _1BitMemLocation u_1bitmemlocation_5 (.Input(in_1[3]), .Clock(Clock), .out_4(Memory[3]), .Enabled(Enabled));
  _1BitMemLocation u_1bitmemlocation_6 (.Input(in_1[2]), .Clock(Clock), .out_4(Memory[2]), .Enabled(Enabled));
  _1BitMemLocation u_1bitmemlocation_7 (.Input(in_1[1]), .Clock(Clock), .out_4(Memory[1]), .Enabled(Enabled));
  _1BitMemLocation u_1bitmemlocation_8 (.Input(in_1[0]), .Clock(Clock), .out_4(Memory[0]), .Enabled(Enabled));

  // Notes on the sheet:
  //   Input
endmodule

module _32BitMemLocation (
  input  [31:0] in_1,
  input  Enabled,
  input  Enable_Output,
  output [31:0] out_4
);

  wire clock_1_out;
  wire [7:0] n8bitmemlocation_1_memory, n8bitmemlocation_2_memory, n8bitmemlocation_3_memory,
       n8bitmemlocation_4_memory;
  wire [31:0] bit_extender_1_out;

  Clock clock_1 (.out(clock_1_out));
  _8BitMemLocation u_8bitmemlocation_1 (
    .in_1(in_1[31:24]), .Clock(clock_1_out), .Enabled(Enabled), .Memory(n8bitmemlocation_1_memory));
  _8BitMemLocation u_8bitmemlocation_2 (
    .in_1(in_1[23:16]), .Clock(clock_1_out), .Enabled(Enabled), .Memory(n8bitmemlocation_2_memory));
  _8BitMemLocation u_8bitmemlocation_3 (
    .in_1(in_1[15:8]), .Clock(clock_1_out), .Enabled(Enabled), .Memory(n8bitmemlocation_3_memory));
  _8BitMemLocation u_8bitmemlocation_4 (
    .in_1(in_1[7:0]), .Clock(clock_1_out), .Enabled(Enabled), .Memory(n8bitmemlocation_4_memory));
  assign bit_extender_1_out = {{31{Enable_Output}}, Enable_Output};  // Bit_Extender bit_extender_1
  assign out_4 = {n8bitmemlocation_1_memory, n8bitmemlocation_2_memory, n8bitmemlocation_3_memory, n8bitmemlocation_4_memory} & bit_extender_1_out;  // AND_Gate and_1, 32 bits wide

  // Notes on the sheet:
  //   Input
  //   Clock
  //   Output
endmodule

module MBR (
  input  [7:0] Input,
  input  Clock,
  input  Signed,
  input  Unsigned,
  output [31:0] out_5,
  output [31:0] out_6
);

  wire [7:0] n8bitmemlocation_1_memory;
  wire [31:0] bit_extender_1_out, bit_extender_2_out, bit_extender_3_out, bit_extender_4_out;

  _8BitMemLocation u_8bitmemlocation_1 (
    .in_1(Input), .Clock(Clock), .Enabled(1'b1), .Memory(n8bitmemlocation_1_memory));
  assign bit_extender_1_out = {{31{Signed}}, Signed};  // Bit_Extender bit_extender_1
  assign bit_extender_2_out = {{24{n8bitmemlocation_1_memory[7]}}, n8bitmemlocation_1_memory};  // Bit_Extender bit_extender_2
  assign bit_extender_3_out = {{24{1'b0}}, n8bitmemlocation_1_memory};  // Bit_Extender bit_extender_3
  assign bit_extender_4_out = {{31{Unsigned}}, Unsigned};  // Bit_Extender bit_extender_4
  assign out_5 = bit_extender_1_out & bit_extender_2_out;  // AND_Gate and_1, 32 bits wide
  assign out_6 = bit_extender_3_out & bit_extender_4_out;  // AND_Gate and_2, 32 bits wide

  // Notes on the sheet:
  //   Signed Output
  //   Unsigned Output
endmodule
