// Logisim project B-Bus.circ as structural Verilog: 26 circuits, main circuit main
// MDR
module main (
);

  wire addr_1_out_2, alu_1_out_4, alu_1_out_5, alu_1_out_6, alu_control_1_p1, alu_control_1_p2,
       alu_control_1_p3, b_1_out_2, c_1_out_2, c_1_out_3, c_1_out_4, c_1_out_5, c_1_out_6, c_1_out_7,
       c_1_out_9, c_1_out_10, decoder_1_out_2, decoder_1_out_3, decoder_1_out_4, decoder_1_out_5,
       decoder_1_out_6, decoder_1_out_7, decoder_1_out_8, decoder_1_out_9, decoder_1_out_10, h_1_out_3,
       high_bit_1_out_4, j_1_out_2, j_1_out_3, m_1_out_2, mar_1_out_3, mar_1_out_4, mbr_1_out_5,
       mpc_1_out_10, o_1_out_4;
  wire [31:0] sp_1_out_4;

  Clock clock_1 ();  // open: out
  MAR mar_1 (.in_1(m_1_out_2), .out_4(mar_1_out_4), .out_3(mar_1_out_3));  // open: in_2
  SP sp_1 (.in_1(mar_1_out_4), .in_2(c_1_out_6), .in_3(decoder_1_out_6), .out_4(sp_1_out_4));
  LV lv_1 (.in_1(mar_1_out_4), .in_2(c_1_out_5), .in_3(decoder_1_out_7), .out_4(sp_1_out_4));
  CPP cpp_1 (.in_1(mar_1_out_4), .in_2(c_1_out_10), .in_3(decoder_1_out_8), .out_4(sp_1_out_4));
  TOS tos_1 (.in_1(mar_1_out_4), .in_2(c_1_out_4), .in_3(decoder_1_out_9), .out_4(sp_1_out_4));
  OPC opc_1 (.in_1(mar_1_out_4), .in_2(c_1_out_9), .in_3(decoder_1_out_10), .out_4(sp_1_out_4));
  H h_1 (.in_1(mar_1_out_4), .in_2(c_1_out_3), .out_3(h_1_out_3));
  MBR mbr_1 (
    .in_1(mar_1_out_4), .in_2(decoder_1_out_5), .in_3(decoder_1_out_4), .out_5(mbr_1_out_5),
    .out_4(sp_1_out_4), .out_6(sp_1_out_4));
  ALU alu_1 (
    .in_1(sp_1_out_4), .in_2(h_1_out_3), .in_3(alu_control_1_p3), .out_6(alu_1_out_6), .out_5(alu_1_out_5),
    .out_4(alu_1_out_4));
  MDR mdr_1 (.in_3(c_1_out_2), .out_4(sp_1_out_4), .in_2(decoder_1_out_2), .in_1(mar_1_out_4));
  PC pc_1 (.in_1(decoder_1_out_3), .in_3(mar_1_out_4), .in_2(c_1_out_7), .in_4(sp_1_out_4));
  SHIFTER shifter_1 (.in_1(alu_1_out_6), .in_2(alu_control_1_p1), .out_3(mar_1_out_4));
  Decoder decoder_1 (
    .in_1(b_1_out_2), .out_2(decoder_1_out_2), .out_3(decoder_1_out_3), .out_4(decoder_1_out_4),
    .out_5(decoder_1_out_5), .out_6(decoder_1_out_6), .out_7(decoder_1_out_7), .out_8(decoder_1_out_8),
    .out_9(decoder_1_out_9), .out_10(decoder_1_out_10));
  O o_1 (.in_1(j_1_out_3), .in_2(addr_1_out_2), .in_3(mbr_1_out_5), .out_4(o_1_out_4));
  High_Bit high_bit_1 (.in_1(j_1_out_2), .in_2(alu_1_out_4), .in_3(alu_1_out_5), .out_4(high_bit_1_out_4));
  MPC mpc_1 (
    .in_1(high_bit_1_out_4), .in_2(o_1_out_4), .in_3(o_1_out_4), .in_4(o_1_out_4), .in_5(o_1_out_4),
    .in_6(o_1_out_4), .in_7(o_1_out_4), .in_8(o_1_out_4), .in_9(o_1_out_4), .out_10(mpc_1_out_10));
  J j_1 (.in_1(alu_control_1_p2), .out_2(j_1_out_2), .out_3(j_1_out_3));
  Addr addr_1 (.in_1(alu_control_1_p2), .out_2(addr_1_out_2));
  // ALU___Control alu_control_1: pin names not known; wires that end beside it: alu_control_1_p1, alu_control_1_p2, alu_control_1_p3
  Control_Store control_store_1 (.in_1(mpc_1_out_10), .out_2(alu_control_1_p2));
  C c_1 (
    .in_1(alu_control_1_p2), .out_3(c_1_out_3), .out_9(c_1_out_9), .out_4(c_1_out_4), .out_10(c_1_out_10),
    .out_5(c_1_out_5), .out_6(c_1_out_6), .out_7(c_1_out_7), .out_2(c_1_out_2), .out_8(mar_1_out_3));
  M m_1 (.in_1(alu_control_1_p2), .out_2(m_1_out_2));
  B b_1 (.in_1(alu_control_1_p2), .out_2(b_1_out_2));
endmodule

module B_Bus (
  input  [31:0] in_1,
  input  [31:0] in_2,
  input  [31:0] in_3,
  input  [31:0] in_4,
  input  [31:0] in_5,
  input  [31:0] in_6,
  input  [31:0] in_7,
  input  [31:0] in_8,
  input  [31:0] in_9,
  output [31:0] out_10
);

  assign out_10 = in_9 | in_8 | in_7 | in_6 | in_5 | in_4 | in_3 | in_2 | in_1;  // OR_Gate or_1, 32 bits wide
endmodule

module MAR (
  input  in_1,
  input  in_2,
  output out_3,
  output out_4
);

  buf or_1 (out_4, in_1);  // OR_Gate
endmodule

module MDR (
  input  in_1,
  input  in_2,
  input  in_3,
  output [31:0] out_4
);
endmodule

module PC (
  input  in_1,
  input  in_2,
  input  in_3,
  input  [31:0] in_4
);
endmodule

module MBR (
  input  in_1,
  input  in_2,
  input  in_3,
  output [31:0] out_4,
  output out_5,
  output [31:0] out_6
);
endmodule

module SP (
  input  in_1,
  input  in_2,
  input  in_3,
  output [31:0] out_4
);
endmodule

module LV (
  input  in_1,
  input  in_2,
  input  in_3,
  output [31:0] out_4
);
endmodule

module CPP (
  input  in_1,
  input  in_2,
  input  in_3,
  output [31:0] out_4
);
endmodule

module TOS (
  input  in_1,
  input  in_2,
  input  in_3,
  output [31:0] out_4
);
endmodule

module OPC (
  input  in_1,
  input  in_2,
  input  in_3,
  output [31:0] out_4
);
endmodule

module H (
  input  in_1,
  input  in_2,
  output out_3
);
endmodule

module ALU (
  input  [31:0] in_1,
  input  in_2,
  input  in_3,
  output out_4,
  output out_5,
  output out_6
);
endmodule

// Shifter
module SHIFTER (
  input  in_1,
  input  in_2,
  output out_3
);
endmodule

module High_Bit (
  input  in_1,
  input  in_2,
  input  in_3,
  output out_4
);
endmodule

module O (
  input  in_1,
  input  in_2,
  input  in_3,
  output out_4
);
endmodule

module MPC (
  input  in_1,
  input  in_2,
  input  in_3,
  input  in_4,
  input  in_5,
  input  in_6,
  input  in_7,
  input  in_8,
  input  in_9,
  output out_10
);
endmodule

module Decoder (
  input  in_1,
  output out_2,
  output out_3,
  output out_4,
  output out_5,
  output out_6,
  output out_7,
  output out_8,
  output out_9,
  output out_10
);
endmodule

module Control_Store (
  input  in_1,
  output out_2
);
endmodule

module Addr (
  input  in_1,
  output out_2
);
endmodule

module J (
  input  in_1,
  output out_2,
  output out_3
);
endmodule

// ALU
module ALU___Control (
  input  in_1,
  output out_2,
  output out_3
);
endmodule

module C (
  input  in_1,
  output out_2,
  output out_3,
  output out_4,
  output out_5,
  output out_6,
  output out_7,
  output out_8,
  output out_9,
  output out_10
);
endmodule

module M (
  input  in_1,
  output out_2
);
endmodule

module B (
  input  in_1,
  output out_2
);
endmodule

module Wired_Machine (
);

  MAR mar_1 ();  // open: in_1, out_4, out_3, in_2
  MBR mbr_1 ();  // open: in_1, in_2, in_3, out_5, out_4, out_6
  SP sp_1 ();  // open: in_1, in_2, in_3, out_4
  LV lv_1 ();  // open: in_1, in_2, in_3, out_4
  CPP cpp_1 ();  // open: in_1, in_2, in_3, out_4
  TOS tos_1 ();  // open: in_1, in_2, in_3, out_4
  OPC opc_1 ();  // open: in_1, in_2, in_3, out_4
  H h_1 ();  // open: in_1, in_2, out_3
  ALU alu_1 ();  // open: in_1, in_2, in_3, out_6, out_5, out_4
  MDR mdr_1 ();  // open: in_3, out_4, in_2, in_1
  PC pc_1 ();  // open: in_1, in_3, in_2, in_4
  SHIFTER shifter_1 ();  // open: in_1, in_2, out_3
  Decoder decoder_1 ();  // open: in_1, out_2, out_3, out_4, out_5, out_6, out_7, out_8, out_9, out_10
  High_Bit high_bit_1 ();  // open: in_1, in_2, in_3, out_4
  MPC mpc_1 ();  // open: in_1, in_2, in_3, in_4, in_5, in_6, in_7, in_8, in_9, out_10
  O o_1 ();  // open: in_1, in_2, in_3, out_4
  Addr addr_1 ();  // open: in_1, out_2
  ALU___Control alu_control_1 ();  // open: in_1, out_2, out_3
  J j_1 ();  // open: in_1, out_2, out_3
  Control_Store control_store_1 ();  // open: in_1, out_2
  C c_1 ();  // open: in_1, out_3, out_9, out_4, out_10, out_5, out_6, out_7, out_2, out_8
  M m_1 ();  // open: in_1, out_2
  B b_1 ();  // open: in_1, out_2
endmodule
