// Logisim project High-Bit.circ as structural Verilog
module High_Bit (
  input  N,
  input  in_2,
  input  [1:0] JAMN_JAMZ,
  input  Z,
  output out_5
);

  wire and_1_out, and_2_out, d_ff_1_q, d_ff_2_q;

  D_Flip_Flop d_ff_1 (.clk(in_2), .D(N), .Q(d_ff_1_q));  // open: Qn, preset, en, reset
  D_Flip_Flop d_ff_2 (.clk(in_2), .D(Z), .Q(d_ff_2_q));  // open: Qn, preset, en, reset
  and and_1 (and_1_out, d_ff_1_q, JAMN_JAMZ[1]);
  and and_2 (and_2_out, JAMN_JAMZ[0], d_ff_2_q);
  or or_1 (out_5, and_1_out, and_2_out);
endmodule
