// Logisim project RAM.circ as structural Verilog
module ByteAddressableRAM (
  input  [23:0] in_1,
  input  Type,
  input  [31:0] in_3,
  input  Clear,
  input  in_5,
  input  in_6,
  output [31:0] out_7,
  output [7:0] MBR
);

  wire decoder_1_out0, decoder_1_out1, decoder_1_out2, decoder_1_out3, not_1_out;
  wire [1:0] counter_1_q;
  wire [7:0] multiplexer_1_out, ram_1_data;
  wire [23:0] controlled_buffer_1_out;

  Counter #(.width(2), .max('h3)) counter_1 (.Q(counter_1_q), .clk(in_5));  // open: load, D, count, carry, clr
  not not_1 (not_1_out, Type);
  Multiplexer #(.select(2), .width(8)) multiplexer_1 (
    .in0(in_3[7:0]), .in1(in_3[15:8]), .in2(in_3[23:16]), .in3(in_3[31:24]), .out(multiplexer_1_out),
    .sel(counter_1_q));  // open: en
  assign controlled_buffer_1_out = not_1_out ? in_1 : 24'bz;  // Controlled_Buffer controlled_buffer_1
  assign controlled_buffer_1_out = Type ? {in_1[21:0], counter_1_q} : 24'bz;  // Controlled_Buffer controlled_buffer_2
  RAM #(.addrWidth(24), .bus("separate")) ram_1 (
    .addr(controlled_buffer_1_out), .din(multiplexer_1_out), .data(ram_1_data), .clk(in_5));  // open: str, sel, ld, clr
  Decoder #(.select(2)) decoder_1 (
    .out0(decoder_1_out0), .out1(decoder_1_out1), .out2(decoder_1_out2), .out3(decoder_1_out3),
    .sel(counter_1_q));  // open: en
  Register #(.trigger("falling")) register_1 (.D(ram_1_data), .Q(MBR), .clk(decoder_1_out0), .clr(Clear));  // open: en
  Register #(.trigger("falling")) register_2 (
    .D(ram_1_data), .Q(out_7[15:8]), .clk(decoder_1_out1), .clr(Clear));  // open: en
  Register #(.trigger("falling")) register_3 (
    .D(ram_1_data), .Q(out_7[23:16]), .clk(decoder_1_out2), .clr(Clear));  // open: en
  Register #(.trigger("falling")) register_4 (
    .D(ram_1_data), .Q(out_7[31:24]), .clk(decoder_1_out3), .clr(Clear));  // open: en

  assign out_7[7:0] = MBR;

  // Notes on the sheet:
  //   0 = byte address
  //   1 = word address
  //   Address
  //   MDR
endmodule

module WordAddressableRAM (
  input  [23:0] in_1,
  input  Type,
  input  [31:0] in_3,
  input  in_4,
  output [31:0] out_5,
  output [7:0] MBR
);

  wire not_1_out;
  wire [23:0] controlled_buffer_1_out;

  assign controlled_buffer_1_out = Type ? in_1 : 24'bz;  // Controlled_Buffer controlled_buffer_1
  not not_1 (not_1_out, Type);
  assign controlled_buffer_1_out = not_1_out ? {2'b00, in_1[23:2]} : 24'bz;  // Controlled_Buffer controlled_buffer_2
  RAM #(.addrWidth(24), .dataWidth(32), .bus("separate")) ram_1 (
    .addr(controlled_buffer_1_out), .din(in_3), .data(out_5), .clk(in_4));  // open: str, sel, ld, clr
  Multiplexer #(.select(2), .width(8)) multiplexer_1 (
    .in0(out_5[31:24]), .in1(out_5[23:16]), .in2(out_5[15:8]), .in3(out_5[7:0]), .out(MBR), .sel(in_1[1:0]));  // open: en

  // Notes on the sheet:
  //   1 = byte addressable
  //   0 = word addressable
  //   Address
  //   MDR
endmodule

module ROM (
  input  [8:0] in_1,
  output [31:0] out_2,
  output [3:0] out_3
);

  ROM_part #(.addrWidth(9), .dataWidth(32)) rom_1 (.addr(in_1), .data(out_2));  // open: sel
  ROM_part #(.addrWidth(9), .dataWidth(4)) rom_2 (.addr(in_1), .data(out_3));  // open: sel
endmodule
